// Logisim project PWM.circ as structural Verilog: 5 circuits, main circuit PWM_Servo
module PWM_Servo (
  input  [7:0] Angle,
  input  EN_HT,
  input  clk,
  input  Reset,
  output SERVO_OUT
);

  wire [25:0] Servo_Mapper_1_out_26b;

  Servo_Mapper Servo_Mapper_1 (.In_8b(Angle), .Out_26b(Servo_Mapper_1_out_26b));
  PWM_Base PWM_Base_1 (
    .High_Time(Servo_Mapper_1_out_26b), .EN_HT(EN_HT), .Period(26'h1312cff), .clk(clk), .Reset(Reset),
    .PWM_OUT(SERVO_OUT));

  // Notes on the sheet:
  //   20[ms]
endmodule

module PWM_Motor (
  input  [7:0] High,
  input  En_H,
  input  clk,
  input  Reset,
  output MOTOR_OUT
);

  wire [25:0] Motor_Mapper_1_out_26b;

  Motor_Mapper Motor_Mapper_1 (.In_8b(High), .Out_26b(Motor_Mapper_1_out_26b));
  PWM_Base PWM_Base_1 (
    .High_Time(Motor_Mapper_1_out_26b), .EN_HT(En_H), .Period(26'h7ff), .clk(clk), .Reset(Reset),
    .PWM_OUT(MOTOR_OUT));
endmodule

module PWM_Base (
  input  [25:0] High_Time,
  input  EN_HT,
  input  [25:0] Period,
  input  clk,
  input  Reset,
  output PWM_OUT
);

  wire comparator_1_eq, comparator_1_gt, or_1_out;
  wire [25:0] cpt, ht;

  Register #(.width(26)) register_1 (.D(High_Time), .en(EN_HT), .clk(clk), .Q(ht), .clr(Reset));
  Comparator #(.width(26), .mode("unsigned")) comparator_1 (
    .a(cpt), .b(Period), .gt(comparator_1_gt), .eq(comparator_1_eq));  // open: lt
  Counter #(.width(26), .max('h3ffffff)) counter_1 (
    .clr(or_1_out), .clk(clk), .Q(cpt));  // open: load, up, count, D, carry
  or or_1 (or_1_out, Reset, comparator_1_gt, comparator_1_eq);
  Comparator #(.width(26), .mode("unsigned")) comparator_2 (.a(cpt), .b(ht), .lt(PWM_OUT));  // open: gt, eq

  // Other names for the same wires on the sheet: p[25:0] = Period; R = Reset
endmodule

module Servo_Mapper (
  input  [7:0] In_8b,
  output [25:0] Out_26b
);

  wire comparator_1_gt, comparator_2_lt, or_1_out;
  wire [25:0] adder_1_out, multiplexer_1_out;

  Comparator #(.mode("unsigned")) comparator_1 (.a(In_8b), .b(8'hfa), .gt(comparator_1_gt));  // open: eq, lt
  Comparator #(.mode("unsigned")) comparator_2 (.a(In_8b), .b(8'h5), .lt(comparator_2_lt));  // open: gt, eq
  Adder #(.width(26)) adder_1 (.a({10'h1, In_8b, {8{1'b0}}}), .b(26'hb768), .out(adder_1_out));  // open: cin, cout
  Multiplexer #(.width(26), .enable("false")) multiplexer_1 (
    .in0(26'h1adb0), .in1(26'h2bf20), .out(multiplexer_1_out), .sel(comparator_1_gt));
  or or_1 (or_1_out, comparator_1_gt, comparator_2_lt);
  Multiplexer #(.width(26), .enable("false")) multiplexer_2 (
    .in0(adder_1_out), .in1(multiplexer_1_out), .out(Out_26b), .sel(or_1_out));
  // Probe on Out_26b
endmodule

module Motor_Mapper (
  input  [7:0] In_8b,
  output [25:0] Out_26b
);

  wire comparator_1_gt;

  Comparator #(.mode("unsigned")) comparator_1 (.a(In_8b), .b(8'hfa), .gt(comparator_1_gt));  // open: eq, lt
  Multiplexer #(.width(11), .enable("false")) multiplexer_1 (
    .in0({1'b0, In_8b, 2'b00}), .in1(11'h598), .out(Out_26b[11:1]), .sel(comparator_1_gt));

  assign {Out_26b[25:12], Out_26b[0]} = {15{1'b0}};

  // Notes on the sheet:
  //   70%
endmodule
