// Logisim project Timer.circ as structural Verilog: 1 circuit, main circuit Timer
module Timer (
  input  [7:0] Sleep_Time,
  input  EN,
  input  CLK,
  input  Reset,
  output [7:0] TimeOut
);

  wire count, or_1_out;
  wire [7:0] val;
  wire [25:0] adder_1_out, register_2_q;

  Register register_1 (.D(Sleep_Time), .en(EN), .clk(CLK), .Q(val), .clr(Reset));
  Adder #(.width(26)) adder_1 (.a(register_2_q), .b(26'h1), .out(adder_1_out));  // open: cin, cout
  Register #(.width(26)) register_2 (.D(adder_1_out), .en(count), .clk(CLK), .Q(register_2_q), .clr(or_1_out));
  or or_1 (or_1_out, Reset, EN);
  Comparator #(.width(26), .mode("unsigned")) comparator_1 (
    .a(register_2_q), .b({val, {18{1'b1}}}), .eq(TimeOut[0]), .lt(count));  // open: gt

  assign TimeOut[7:1] = {7{1'b0}};

  // Other names for the same wires on the sheet: ld = EN; R = Reset
endmodule
