// Logisim project UART_8bit.circ as structural Verilog: 3 circuits, main circuit Send
module Network_Card (
  input  [7:0] Data_In,
  input  LD_D,
  input  UART_INPUT,
  input  clk,
  input  Reset,
  output UART_OUTPUT,
  output [7:0] Data_Out,
  output [7:0] Online
);

  wire and_1_out, counter_1_carry, or_1_out, or_2_out, Rec;
  wire [7:0] register_1_q;

  Register register_1 (.D(Data_In), .en(LD_D), .clk(clk), .Q(register_1_q));  // open: clr
  Counter #(.width(27), .max('h5f5e100), .ongoal("stay")) counter_1 (
    .clr(or_1_out), .clk(clk), .carry(counter_1_carry));  // open: load, up, count, D, Q
  or or_1 (or_1_out, Rec, Reset);
  Send send_1 (.Data_In(register_1_q), .CLK(clk), .Reset(Reset), .UART_OUTPUT(UART_OUTPUT));  // open: LD
  Receive receive_1 (.UART_INPUT(UART_INPUT), .clk(clk), .Reset(Reset), .Value(Data_Out), .Received(Rec));
  and and_1 (and_1_out, ~counter_1_carry, Online[0]);  // AND_Gate
  D_Flip_Flop d_ff_1 (.D(or_2_out), .clk(clk), .Q(Online[0]));  // open: Qn, preset, reset
  or or_2 (or_2_out, Rec, and_1_out);

  assign Online[7:1] = {7{1'b0}};

  // Other names for the same wires on the sheet: R = Reset; U_INP = UART_INPUT
endmodule

module Send (
  input  [7:0] Data_In,
  input  LD,
  input  CLK,
  input  Reset,
  output UART_OUTPUT
);

  wire and_2_out, b, end_s, ld_t, Nb_Shifts_carry, or_1_out, or_2_out, or_3_out, or_4_out, shift,
       shift_register_1_p15;

  Clock clock_1 ();  // open: out
  Clock sysclk ();  // open: out
  or or_1 (or_1_out, Reset, ld_t);
  Counter #(.width(14), .max('h28b0)) Time_Base (
    .clr(or_1_out), .clk(CLK), .carry(shift));  // open: load, up, count, D, Q
  and and_1 (ld_t, ~b, LD);  // AND_Gate
  // Probe on ld_t
  // Shift_Register #(.length(9)) shift_register_1: pin names not known; wires that end beside it: Reset, ld_t, shift, CLK, 1'b1, Data_In[0], Data_In[1], Data_In[2], Data_In[3], Data_In[4], Data_In[5], Data_In[6], Data_In[7], 1'b0, shift_register_1_p15
  // Probe on shift
  Counter #(.width(4), .max('h9)) Nb_Shifts (
    .clr(or_2_out), .count(shift), .clk(CLK), .carry(Nb_Shifts_carry));  // open: load, up, D, Q
  or or_2 (or_2_out, Reset, ld_t);
  and and_2 (and_2_out, b, ~end_s);  // AND_Gate
  or or_3 (or_3_out, ld_t, and_2_out);
  D_Flip_Flop Busy (.D(or_3_out), .clk(CLK), .Q(b), .reset(or_4_out));  // open: Qn, preset
  or or_4 (or_4_out, end_s, Reset);
  Multiplexer #(.enable("false")) multiplexer_1 (.in0(1'b1), .in1(shift_register_1_p15), .out(UART_OUTPUT), .sel(b));
  and and_3 (end_s, shift, Nb_Shifts_carry);

  // Other names for the same wires on the sheet: data[7:0] = Data_In; R = Reset
endmodule

module Receive (
  input  UART_INPUT,
  input  clk,
  input  Reset,
  output [7:0] Value,
  output Received
);

  wire and_1_out, and_2_out, and_3_out, and_5_out, and_7_out, dephased, end_rec, half, incomming, inp,
       Nb_Shifts_carry, not_1_out, or_1_out, or_2_out, or_4_out, or_5_out, rec, shift, Shift_p1, Shift_p5,
       start;
  wire [7:0] multiplexer_1_out, received_t;
  wire [13:0] Time_Base_q;

  not not_1 (not_1_out, UART_INPUT);
  and and_1 (and_1_out, start, ~rec);  // AND_Gate
  nor nor_1 (incomming, rec, inp, start);
  D_Flip_Flop Input (.D(not_1_out), .clk(clk), .Qn(inp), .reset(Reset));  // open: Q, preset
  D_Flip_Flop u_start (.D(or_1_out), .clk(clk), .Q(start), .reset(Reset));  // open: Qn, preset
  or or_1 (or_1_out, and_1_out, incomming);
  Counter #(.width(14), .max('h28b0)) Time_Base (
    .clr(Reset), .load(or_2_out), .clk(clk), .D(14'h1), .carry(shift), .Q(Time_Base_q));  // open: up, count
  or or_2 (or_2_out, incomming, dephased);
  // Probe on inp
  // Shift_Register #(.length(9)) Shift: pin names not known; wires that end beside it: Shift_p1, shift, clk, inp, Shift_p5, received_t[7], received_t[6], received_t[5], received_t[4], received_t[3], received_t[2], received_t[1], received_t[0]
  or or_3 (Shift_p1, start, Reset);
  // Probe on shift
  and and_2 (and_2_out, ~Time_Base_q[0], ~Time_Base_q[1], ~Time_Base_q[2], Time_Base_q[3], Time_Base_q[4], ~Time_Base_q[5], Time_Base_q[6], ~Time_Base_q[7], ~Time_Base_q[8], ~Time_Base_q[9], Time_Base_q[10], ~Time_Base_q[11], Time_Base_q[12]);  // AND_Gate
  // Probe on received_t
  D_Flip_Flop u_Half (.D(and_2_out), .clk(clk), .Q(half), .reset(Reset));  // open: Qn, preset
  and and_3 (and_3_out, Shift_p5, end_rec);
  Register Last_Value (.D(multiplexer_1_out), .en(rec), .clk(clk), .Q(Value), .clr(Reset));
  Multiplexer #(.width(8), .enable("false")) multiplexer_1 (
    .in0(Value), .in1(received_t), .out(multiplexer_1_out), .sel(and_3_out));
  and and_4 (dephased, start, half);
  and and_5 (and_5_out, rec, ~end_rec);  // AND_Gate
  Counter #(.width(4), .max('h8)) Nb_Shifts (
    .clr(or_4_out), .count(shift), .clk(clk), .carry(Nb_Shifts_carry));  // open: load, up, D, Q
  or or_4 (or_4_out, Reset, incomming);
  and and_6 (Received, ~or_5_out, rec);  // AND_Gate
  D_Flip_Flop Receiving (.D(or_5_out), .clk(clk), .Q(rec), .reset(Reset));  // open: Qn, preset
  or or_5 (or_5_out, dephased, and_5_out);
  D_Flip_Flop d_ff_1 (.D(and_7_out), .clk(clk), .Q(end_rec), .reset(Reset));  // open: Qn, preset
  and and_7 (and_7_out, shift, Nb_Shifts_carry);

  // Other names for the same wires on the sheet: R = Reset

  // Notes on the sheet:
  //   Evite le chargement accidentel au démarrage
endmodule
